// Logisim project ComputerTest.circ as structural Verilog
module main (
  input  [25:0] Address,
  input  [31:0] Data,
  input  [2:0] func3,
  output [31:0] LoadData
);

  wire clock_1_out, dipswitch_1_sw1, dipswitch_1_sw2, not_1_out;
  wire [31:0] ram_1_dout, ram_setter_1_bytestore, transistor_1_out;

  DipSwitch #(.number(2)) dipswitch_1 (.sw1(dipswitch_1_sw1), .sw2(dipswitch_1_sw2));
  Clock clock_1 (.out(clock_1_out));
  not not_1 (not_1_out, 1'b1);
  RAM #(.addrWidth(24), .dataWidth(32)) ram_1 (
    .addr(Address[25:2]), .we(dipswitch_1_sw2), .oe(1'b1), .clk(clock_1_out), .din(ram_setter_1_bytestore),
    .dout(ram_1_dout));
  Transistor #(.width(32)) transistor_1 (.in(Data), .out(transistor_1_out), .gate(not_1_out));
  RAM_SETTER ram_setter_1 (
    .DATA(transistor_1_out), .MEMORY(ram_1_dout), .FUNC3(func3), .BYTELOCATION(Address[1:0]),
    .LOAD(dipswitch_1_sw1), .ByteStore(ram_setter_1_bytestore), .ByteLoad(LoadData));

  // Notes on the sheet:
  //   Load
  //   Store
endmodule

module ALU (
  input  [6:0] func7,
  input  [31:0] rs1,
  input  [31:0] rs2,
  input  [2:0] func3,
  input  immediate,
  output [31:0] rd
);

  wire and_2_out, comparator_1_gt, comparator_2_gt, not_1_out;
  wire [31:0] adder_1_out, and_1_out, bit_extender_1_out, bit_extender_2_out, multiplexer_1_out,
       multiplexer_2_out, or_1_out, shifter_1_out, shifter_2_out, shifter_3_out, subtractor_1_out, xor_1_out;

  not not_1 (not_1_out, immediate);
  Adder #(.width(32)) adder_1 (.a(rs1), .b(rs2), .out(adder_1_out));  // open: cin, cout
  Subtractor #(.width(32)) subtractor_1 (.a(rs1), .b(rs2), .out(subtractor_1_out));  // open: bin, bout
  Shifter #(.width(32)) shifter_1 (.in(rs2), .\dist (rs2[4:0]), .out(shifter_1_out));
  Comparator #(.width(32)) comparator_1 (.a(rs1), .b(rs2), .gt(comparator_1_gt));  // open: eq, lt
  Comparator #(.mode("unsigned"), .width(32)) comparator_2 (.a(rs2), .b(rs2), .gt(comparator_2_gt));  // open: eq, lt
  assign xor_1_out = rs1 ^ rs2;  // XOR_Gate xor_1, 32 bits wide
  Shifter #(.shift("lr"), .width(32)) shifter_2 (.in(rs1), .\dist (rs2[4:0]), .out(shifter_2_out));
  Shifter #(.shift("ar"), .width(32)) shifter_3 (.in(rs1), .\dist (rs2[4:0]), .out(shifter_3_out));
  assign bit_extender_1_out = {{31{comparator_1_gt}}, comparator_1_gt};  // Bit_Extender bit_extender_1
  assign bit_extender_2_out = {{31{comparator_2_gt}}, comparator_2_gt};  // Bit_Extender bit_extender_2
  assign or_1_out = rs1 | rs2;  // OR_Gate or_1, 32 bits wide
  assign and_1_out = rs1 & rs2;  // AND_Gate and_1, 32 bits wide
  Multiplexer #(.width(32)) multiplexer_1 (
    .in0(adder_1_out), .in1(subtractor_1_out), .out(multiplexer_1_out), .sel(and_2_out));
  Multiplexer #(.width(32)) multiplexer_2 (
    .in0(shifter_2_out), .in1(shifter_3_out), .out(multiplexer_2_out), .sel(and_2_out));
  and and_2 (and_2_out, func7[5], not_1_out);
  Multiplexer #(.select(3), .width(32)) multiplexer_3 (
    .in0(multiplexer_1_out), .in1(shifter_1_out), .in2(bit_extender_1_out), .in3(bit_extender_2_out),
    .in4(xor_1_out), .in5(multiplexer_2_out), .in6(or_1_out), .in7(and_1_out), .out(rd), .sel(func3));
endmodule

module RAM_SETTER (
  input  [31:0] DATA,
  input  [31:0] MEMORY,
  input  [2:0] FUNC3,
  input  [1:0] BYTELOCATION,
  input  LOAD,
  output [31:0] ByteStore,
  output [31:0] ByteLoad
);

  wire [7:0] multiplexer_3_out;
  wire [15:0] multiplexer_4_out;
  wire [31:0] bit_extender_1_out, bit_extender_2_out, bit_extender_3_out, multiplexer_1_out,
       multiplexer_2_out, multiplexer_5_out, multiplexer_6_out;

  assign bit_extender_1_out = {{31{LOAD}}, LOAD};  // Bit_Extender bit_extender_1
  Multiplexer #(.width(32)) multiplexer_1 (
    .in0({MEMORY[31:16], DATA[15:0]}), .in1({DATA[15:0], MEMORY[15:0]}), .out(multiplexer_1_out),
    .sel(BYTELOCATION[1]));
  Multiplexer #(.select(2), .width(32)) multiplexer_2 (
    .in0({MEMORY[31:8], DATA[7:0]}), .in1({MEMORY[31:16], DATA[7:0], MEMORY[7:0]}),
    .in2({MEMORY[31:24], DATA[7:0], MEMORY[15:0]}), .in3({DATA[7:0], MEMORY[23:0]}), .out(multiplexer_2_out),
    .sel(BYTELOCATION));
  Multiplexer #(.select(2), .width(8)) multiplexer_3 (
    .in0(MEMORY[7:0]), .in1(MEMORY[15:8]), .in2(MEMORY[23:16]), .in3(MEMORY[31:24]), .out(multiplexer_3_out),
    .sel(BYTELOCATION));
  Multiplexer #(.width(16)) multiplexer_4 (
    .in0(MEMORY[15:0]), .in1(MEMORY[31:16]), .out(multiplexer_4_out), .sel(BYTELOCATION[1]));
  assign bit_extender_2_out = {{24{multiplexer_3_out[7]}}, multiplexer_3_out};  // Bit_Extender bit_extender_2
  assign bit_extender_3_out = {{16{multiplexer_4_out[15]}}, multiplexer_4_out};  // Bit_Extender bit_extender_3
  Multiplexer #(.select(3), .width(32)) multiplexer_5 (
    .in0(multiplexer_2_out), .in1(multiplexer_1_out), .in2(DATA), .out(multiplexer_5_out), .sel(FUNC3));  // open: in3, in4, in5, in6, in7
  assign ByteStore = {32{1'b0}} | multiplexer_5_out;  // OR_Gate or_1, 32 bits wide
  Multiplexer #(.select(3), .width(32)) multiplexer_6 (
    .in0(bit_extender_2_out), .in1(bit_extender_3_out), .in2(MEMORY), .out(multiplexer_6_out), .sel(FUNC3));  // open: in3, in4, in5, in6, in7
  assign ByteLoad = multiplexer_6_out & bit_extender_1_out;  // AND_Gate and_1, 32 bits wide
endmodule

module Registers (
  input  [4:0] rs1,
  input  [4:0] rs2,
  input  [4:0] rd,
  input  [31:0] data,
  input  clock,
  output [31:0] Out1,
  output [31:0] Out2,
  output [31:0] PC
);

  wire r11, r12, r13, r14, r15, r16, r17, r18, r19, r21, r22, r23, r24, r25, r26, r27, r28, r29, r32, r33,
       r34, r35, r36, r37, r38, r39, r110, r111, r112, r113, r114, r115, r116, r117, r118, r119, r120, r121,
       r122, r123, r124, r125, r126, r127, r128, r129, r130, r131, r132, r210, r211, r212, r213, r214, r215,
       r216, r217, r218, r219, r220, r221, r222, r223, r224, r225, r226, r227, r228, r229, r230, r231, r232,
       r310, r311, r312, r313, r314, r315, r316, r317, r318, r319, r320, r321, r322, r323, r324, r325, r326,
       r327, r328, r329, r330, r331, r332;
  wire [31:0] register_1_q, register_2_q, register_3_q, register_4_q, register_5_q, register_6_q,
       register_7_q, register_8_q, register_9_q, register_10_q, register_11_q, register_12_q, register_13_q,
       register_14_q, register_15_q, register_16_q, register_17_q, register_18_q, register_19_q,
       register_20_q, register_21_q, register_22_q, register_23_q, register_24_q, register_25_q,
       register_26_q, register_27_q, register_28_q, register_29_q, register_30_q;

  Demultiplexer #(.select(5)) demultiplexer_1 (
    .out0(r11), .out1(r12), .out2(r13), .out3(r14), .out4(r15), .out5(r16), .out6(r17), .out7(r18),
    .out8(r19), .out9(r110), .out10(r111), .out11(r112), .out12(r113), .out13(r114), .out14(r115),
    .out15(r116), .out16(r117), .out17(r118), .out18(r119), .out19(r120), .out20(r121), .out21(r122),
    .out22(r123), .out23(r124), .out24(r125), .out25(r126), .out26(r127), .out27(r128), .out28(r129),
    .out29(r130), .out30(r131), .out31(r132), .in(1'b1), .sel(rs1));
  Demultiplexer #(.select(5)) demultiplexer_2 (
    .out1(r32), .out2(r33), .out3(r34), .out4(r35), .out5(r36), .out6(r37), .out7(r38), .out8(r39),
    .out9(r310), .out10(r311), .out11(r312), .out12(r313), .out13(r314), .out14(r315), .out15(r316),
    .out16(r317), .out17(r318), .out18(r319), .out19(r320), .out20(r321), .out21(r322), .out22(r323),
    .out23(r324), .out24(r325), .out25(r326), .out26(r327), .out27(r328), .out28(r329), .out29(r330),
    .out30(r331), .out31(r332), .in(1'b1), .sel(rd));  // open: out0
  Demultiplexer #(.select(5)) demultiplexer_3 (
    .out0(r21), .out1(r22), .out2(r23), .out3(r24), .out4(r25), .out5(r26), .out6(r27), .out7(r28),
    .out8(r29), .out9(r210), .out10(r211), .out11(r212), .out12(r213), .out13(r214), .out14(r215),
    .out15(r216), .out16(r217), .out17(r218), .out18(r219), .out19(r220), .out20(r221), .out21(r222),
    .out22(r223), .out23(r224), .out24(r225), .out25(r226), .out26(r227), .out27(r228), .out28(r229),
    .out29(r230), .out30(r231), .out31(r232), .in(1'b1), .sel(rs2));
  Register #(.width(32)) register_1 (.D(data), .en(r322), .clk(clock), .Q(register_1_q));  // open: clr
  Register #(.width(32)) register_2 (.D(data), .en(r323), .clk(clock), .Q(register_2_q));  // open: clr
  Register #(.width(32)) register_3 (.D(data), .en(r324), .clk(clock), .Q(register_3_q));  // open: clr
  Register #(.width(32)) register_4 (.D(data), .en(r325), .clk(clock), .Q(register_4_q));  // open: clr
  Register #(.width(32)) register_5 (.D(data), .en(r326), .clk(clock), .Q(register_5_q));  // open: clr
  Register #(.width(32)) register_6 (.D(data), .en(r327), .clk(clock), .Q(register_6_q));  // open: clr
  Register #(.width(32)) register_7 (.D(data), .en(r328), .clk(clock), .Q(register_7_q));  // open: clr
  Register #(.width(32)) register_8 (.D(data), .en(r329), .clk(clock), .Q(register_8_q));  // open: clr
  Register #(.width(32)) register_9 (.D(data), .en(r330), .clk(clock), .Q(register_9_q));  // open: clr
  Register #(.width(32)) register_10 (.D(data), .en(r331), .clk(clock), .Q(register_10_q));  // open: clr
  Counter #(.max('hffffffff), .width(32)) counter_1 (
    .load(r332), .clk(clock), .D(data), .Q(PC));  // open: clr, up, count, carry
  Register #(.width(32)) register_11 (.D(data), .en(r32), .clk(clock), .Q(register_11_q));  // open: clr
  Register #(.width(32)) register_12 (.D(data), .en(r33), .clk(clock), .Q(register_12_q));  // open: clr
  Register #(.width(32)) register_13 (.D(data), .en(r34), .clk(clock), .Q(register_13_q));  // open: clr
  Register #(.width(32)) register_14 (.D(data), .en(r35), .clk(clock), .Q(register_14_q));  // open: clr
  Register #(.width(32)) register_15 (.D(data), .en(r36), .clk(clock), .Q(register_15_q));  // open: clr
  Register #(.width(32)) register_16 (.D(data), .en(r37), .clk(clock), .Q(register_16_q));  // open: clr
  Register #(.width(32)) register_17 (.D(data), .en(r38), .clk(clock), .Q(register_17_q));  // open: clr
  Register #(.width(32)) register_18 (.D(data), .en(r39), .clk(clock), .Q(register_18_q));  // open: clr
  Register #(.width(32)) register_19 (.D(data), .en(r310), .clk(clock), .Q(register_19_q));  // open: clr
  Register #(.width(32)) register_20 (.D(data), .en(r311), .clk(clock), .Q(register_20_q));  // open: clr
  Register #(.width(32)) register_21 (.D(data), .en(r312), .clk(clock), .Q(register_21_q));  // open: clr
  Register #(.width(32)) register_22 (.D(data), .en(r313), .clk(clock), .Q(register_22_q));  // open: clr
  Register #(.width(32)) register_23 (.D(data), .en(r314), .clk(clock), .Q(register_23_q));  // open: clr
  Register #(.width(32)) register_24 (.D(data), .en(r315), .clk(clock), .Q(register_24_q));  // open: clr
  Register #(.width(32)) register_25 (.D(data), .en(r316), .clk(clock), .Q(register_25_q));  // open: clr
  Register #(.width(32)) register_26 (.D(data), .en(r317), .clk(clock), .Q(register_26_q));  // open: clr
  Register #(.width(32)) register_27 (.D(data), .en(r318), .clk(clock), .Q(register_27_q));  // open: clr
  Register #(.width(32)) register_28 (.D(data), .en(r319), .clk(clock), .Q(register_28_q));  // open: clr
  Register #(.width(32)) register_29 (.D(data), .en(r320), .clk(clock), .Q(register_29_q));  // open: clr
  Register #(.width(32)) register_30 (.D(data), .en(r321), .clk(clock), .Q(register_30_q));  // open: clr
  // bigtransistor bigtransistor_1: pin names not known; wires that end beside it: {32{1'b0}}, {32{1'b0}}, r11, r21, Out1
  // bigtransistor bigtransistor_2: pin names not known; wires that end beside it: {32{1'b0}}, r21, Out2
  // bigtransistor bigtransistor_3: pin names not known; wires that end beside it: register_11_q, r12, register_11_q, Out1, r22
  // bigtransistor bigtransistor_4: pin names not known; wires that end beside it: register_11_q, r22, Out2
  // bigtransistor bigtransistor_5: pin names not known; wires that end beside it: register_12_q, r13, r23, Out1
  // bigtransistor bigtransistor_6: pin names not known; wires that end beside it: register_12_q, r23, Out2
  // bigtransistor bigtransistor_7: pin names not known; wires that end beside it: register_13_q, r14, r24, Out1
  // bigtransistor bigtransistor_8: pin names not known; wires that end beside it: register_13_q, r24, Out2
  // bigtransistor bigtransistor_9: pin names not known; wires that end beside it: r15, Out1
  // bigtransistor bigtransistor_10: pin names not known; wires that end beside it: register_14_q, r16, r25, Out2
  // bigtransistor bigtransistor_11: pin names not known; wires that end beside it: r16, register_15_q, Out1, r26
  // bigtransistor bigtransistor_12: pin names not known; wires that end beside it: register_15_q, r26, Out2
  // bigtransistor bigtransistor_13: pin names not known; wires that end beside it: register_16_q, r17, register_16_q, Out1, r27
  // bigtransistor bigtransistor_14: pin names not known; wires that end beside it: register_16_q, r27, Out2
  // bigtransistor bigtransistor_15: pin names not known; wires that end beside it: register_17_q, r18, r28, Out1
  // bigtransistor bigtransistor_16: pin names not known; wires that end beside it: register_17_q, r28, Out2
  // bigtransistor bigtransistor_17: pin names not known; wires that end beside it: register_18_q, r19, r29, Out1
  // bigtransistor bigtransistor_18: pin names not known; wires that end beside it: register_18_q, r29, Out2
  // bigtransistor bigtransistor_19: pin names not known; wires that end beside it: r110, Out1
  // bigtransistor bigtransistor_20: pin names not known; wires that end beside it: register_19_q, r111, r210, Out2
  // bigtransistor bigtransistor_21: pin names not known; wires that end beside it: r111, register_20_q, Out1, r211
  // bigtransistor bigtransistor_22: pin names not known; wires that end beside it: register_20_q, r211, Out2
  // bigtransistor bigtransistor_23: pin names not known; wires that end beside it: register_21_q, r112, register_21_q, Out1, r212
  // bigtransistor bigtransistor_24: pin names not known; wires that end beside it: register_21_q, r212, Out2
  // bigtransistor bigtransistor_25: pin names not known; wires that end beside it: register_22_q, r113, r213, Out1
  // bigtransistor bigtransistor_26: pin names not known; wires that end beside it: register_22_q, r213, Out2
  // bigtransistor bigtransistor_27: pin names not known; wires that end beside it: register_23_q, r114, r214, Out1
  // bigtransistor bigtransistor_28: pin names not known; wires that end beside it: register_23_q, r214, Out2
  // bigtransistor bigtransistor_29: pin names not known; wires that end beside it: r115, Out1
  // bigtransistor bigtransistor_30: pin names not known; wires that end beside it: register_24_q, r116, r215, Out2
  // bigtransistor bigtransistor_31: pin names not known; wires that end beside it: r116, register_25_q, Out1, r216
  // bigtransistor bigtransistor_32: pin names not known; wires that end beside it: register_25_q, r216, Out2
  // bigtransistor bigtransistor_33: pin names not known; wires that end beside it: register_26_q, r117, register_26_q, Out1, r217
  // bigtransistor bigtransistor_34: pin names not known; wires that end beside it: register_26_q, r217, Out2
  // bigtransistor bigtransistor_35: pin names not known; wires that end beside it: register_27_q, r118, r218, Out1
  // bigtransistor bigtransistor_36: pin names not known; wires that end beside it: register_27_q, r218, Out2
  // bigtransistor bigtransistor_37: pin names not known; wires that end beside it: register_28_q, r119, r219, Out1
  // bigtransistor bigtransistor_38: pin names not known; wires that end beside it: register_28_q, r219, Out2
  // bigtransistor bigtransistor_39: pin names not known; wires that end beside it: r120, Out1
  // bigtransistor bigtransistor_40: pin names not known; wires that end beside it: register_29_q, r121, r220, Out2
  // bigtransistor bigtransistor_41: pin names not known; wires that end beside it: r121, register_30_q, Out1, r221
  // bigtransistor bigtransistor_42: pin names not known; wires that end beside it: register_30_q, r221, Out2
  // bigtransistor bigtransistor_43: pin names not known; wires that end beside it: register_1_q, r122, register_1_q, Out1, r222
  // bigtransistor bigtransistor_44: pin names not known; wires that end beside it: register_1_q, r222, Out2
  // bigtransistor bigtransistor_45: pin names not known; wires that end beside it: register_2_q, r123, r223, Out1
  // bigtransistor bigtransistor_46: pin names not known; wires that end beside it: register_2_q, r223, Out2
  // bigtransistor bigtransistor_47: pin names not known; wires that end beside it: register_3_q, r124, r224, Out1
  // bigtransistor bigtransistor_48: pin names not known; wires that end beside it: register_3_q, r224, Out2
  // bigtransistor bigtransistor_49: pin names not known; wires that end beside it: r125, Out1
  // bigtransistor bigtransistor_50: pin names not known; wires that end beside it: register_4_q, r126, r225, Out2
  // bigtransistor bigtransistor_51: pin names not known; wires that end beside it: r126, register_5_q, Out1, r226
  // bigtransistor bigtransistor_52: pin names not known; wires that end beside it: register_5_q, r226, Out2
  // bigtransistor bigtransistor_53: pin names not known; wires that end beside it: register_6_q, r127, register_6_q, Out1, r227
  // bigtransistor bigtransistor_54: pin names not known; wires that end beside it: register_6_q, r227, Out2
  // bigtransistor bigtransistor_55: pin names not known; wires that end beside it: register_7_q, r128, r228, Out1
  // bigtransistor bigtransistor_56: pin names not known; wires that end beside it: register_7_q, r228, Out2
  // bigtransistor bigtransistor_57: pin names not known; wires that end beside it: register_8_q, r129, r229, Out1
  // bigtransistor bigtransistor_58: pin names not known; wires that end beside it: register_8_q, r229, Out2
  // bigtransistor bigtransistor_59: pin names not known; wires that end beside it: r130, Out1
  // bigtransistor bigtransistor_60: pin names not known; wires that end beside it: register_9_q, r230, r131, Out2
  // bigtransistor bigtransistor_61: pin names not known; wires that end beside it: r131, register_10_q, Out1, r231
  // bigtransistor bigtransistor_62: pin names not known; wires that end beside it: register_10_q, r231, Out2
  // bigtransistor bigtransistor_63: pin names not known; wires that end beside it: PC, r132, PC, Out1, r232
  // bigtransistor bigtransistor_64: pin names not known; wires that end beside it: PC, r232, Out2
endmodule

module bigtransistor (
  input  Gate,
  input  [31:0] Source,
  output [31:0] Drain
);

  wire not_1_out;
  wire [31:0] and_1_out, bit_extender_1_out;

  assign bit_extender_1_out = {{31{Gate}}, Gate};  // Bit_Extender bit_extender_1
  not not_1 (not_1_out, Gate);
  assign and_1_out = bit_extender_1_out & Source;  // AND_Gate and_1, 32 bits wide
  Multiplexer #(.width(32)) multiplexer_1 (.in0(and_1_out), .out(Drain), .sel(not_1_out));  // open: in1
endmodule

module cpu (
  input  [31:0] in_1,
  input  [4:0] in_2,
  input  [4:0] rs2,
  input  [4:0] rd,
  input  in_5,
  input  in_6,
  output [31:0] out_7,
  output [31:0] out_8
);

  wire button_1_out, clock_1_out;
  wire [31:0] alu_1_rd, multiplexer_1_out;

  Clock clock_1 (.out(clock_1_out));
  Button button_1 (.out(button_1_out));
  Multiplexer #(.width(32)) multiplexer_1 (.in0(alu_1_rd), .in1(in_1), .out(multiplexer_1_out), .sel(button_1_out));
  registers_v2 registers_v2_1 (
    .data(multiplexer_1_out), .rs1(in_2), .rs2(rs2), .rd(rd), .store(in_5), .load(in_6), .clock(clock_1_out),
    .rs1out(out_7), .rs2out(out_8));  // open: jump, pc
  ALU alu_1 (.rs1(out_7), .rs2(out_8), .rd(alu_1_rd));  // open: func7, func3, immediate

  // Notes on the sheet:
  //   rs1
endmodule

module registers_v2 (
  input  [31:0] data,
  input  [4:0] rs1,
  input  [4:0] rs2,
  input  [4:0] rd,
  input  store,
  input  load,
  input  clock,
  input  jump,
  output [31:0] rs1out,
  output [31:0] rs2out,
  output [31:0] pc
);

  wire and_1_out, and_2_out, and_3_out, and_4_out, and_5_out, and_6_out, and_7_out, and_8_out, d_ff_1_q,
       nor_1_out, nor_2_out, nor_3_out, nor_4_out, not_1_out;
  wire [4:0] multiplexer_1_out, multiplexer_2_out;
  wire [31:0] ram_1_dout, ram_2_dout, register_1_q;

  and and_1 (and_1_out, rs1[0], rs1[1], rs1[2], rs1[3], rs1[4], and_6_out);
  nor nor_1 (nor_1_out, rs1[0], rs1[1], rs1[2], rs1[3], rs1[4]);
  nor nor_2 (nor_2_out, rs2[0], rs2[1], rs2[2], rs2[3], rs2[4]);
  and and_2 (and_2_out, rs2[0], rs2[1], rs2[2], rs2[3], rs2[4], and_6_out);
  and and_3 (and_3_out, and_6_out, nor_1_out);
  D_Flip_Flop d_ff_1 (.D(store), .clk(not_1_out), .Q(d_ff_1_q));  // open: Qn, preset, reset
  and and_4 (and_4_out, and_6_out, nor_2_out);
  Register #(.width(32)) register_1 (.D(data), .en(not_1_out), .clk(not_1_out), .Q(register_1_q));  // open: clr
  and and_5 (and_5_out, d_ff_1_q, not_1_out);
  and and_6 (and_6_out, load, clock);
  not not_1 (not_1_out, clock);
  RAM #(.addrWidth(5), .dataWidth(32), .trigger("high")) ram_1 (
    .addr(multiplexer_1_out), .we(and_5_out), .oe(and_6_out), .din(register_1_q), .dout(ram_1_dout));
  Multiplexer #(.width(5)) multiplexer_1 (.in0(rs1), .in1(rd), .out(multiplexer_1_out), .sel(not_1_out));
  RAM #(.addrWidth(5), .dataWidth(32), .trigger("high")) ram_2 (
    .addr(multiplexer_2_out), .we(and_5_out), .oe(and_6_out), .din(register_1_q), .dout(ram_2_dout));
  Multiplexer #(.width(5)) multiplexer_2 (.in0(rs2), .in1(rd), .out(multiplexer_2_out), .sel(not_1_out));
  nor nor_3 (nor_3_out, and_4_out, and_2_out);
  Counter #(.max('hffffffff), .width(32)) counter_1 (
    .load(jump), .D(register_1_q), .Q(pc), .clk(clock));  // open: count, carry, up, clr
  nor nor_4 (nor_4_out, and_1_out, and_3_out);
  assign rs1out = and_8_out ? ram_1_dout : 32'bz;  // Controlled_Buffer controlled_buffer_1
  assign rs2out = and_7_out ? ram_2_dout : 32'bz;  // Controlled_Buffer controlled_buffer_2
  and and_7 (and_7_out, nor_3_out, and_6_out);
  assign rs1out = and_3_out ? {32{1'b0}} : 32'bz;  // Controlled_Buffer controlled_buffer_3
  assign rs1out = and_1_out ? pc : 32'bz;  // Controlled_Buffer controlled_buffer_4
  and and_8 (and_8_out, nor_4_out, and_6_out);
  assign rs2out = and_2_out ? pc : 32'bz;  // Controlled_Buffer controlled_buffer_5
  assign rs2out = and_4_out ? {32{1'b0}} : 32'bz;  // Controlled_Buffer controlled_buffer_6
endmodule
