// Logisim project ComputerV1.circ as structural Verilog: 8 circuits, main circuit main
module main (
);

  wire clock_1_out;
  wire [7:0] program_counter_q;
  wire [31:0] program_data;

  Clock clock_1 (.out(clock_1_out));
  Counter program_counter (.up(1'b1), .clk(clock_1_out), .Q(program_counter_q));  // open: clr, load, count, D, carry
  ROM #(.dataWidth(32)) \program  (.addr(program_counter_q), .data(program_data));
  cpu cpu_1 (.instruction(program_data));

  // Notes on the sheet:
  //   contents of program (hex, n*v repeats v):
  //   ff00193 f1f113 ff14093 f0e193 208233 40320233 11f233 226233 324233 112233 12213 113233 13213 400293
  //   511233 525233 421213 425213 425233 4012d293 4052d2b3 1237 217 26f 420267 7213 21463 6f 100463 6f
  //   115463 6f 20f463 6f 24463 6f 26463 6f 300223 3002a3 300323 3003a3 400203 2223 402203
endmodule

module cpu (
  input  [31:0] instruction
);

  wire [4:0] alu_immediate_rd, alu_immediate_rs1, alu_rd, alu_rs1, alu_rs2, branch_rs1, branch_rs2, load_rd,
       load_rs1, store_rs1, store_rs2;
  wire [24:0] demultiplexer_1_out0, demultiplexer_2_out0, demultiplexer_2_out1, demultiplexer_2_out2,
       demultiplexer_2_out3, demultiplexer_2_out6;

  // Probe on instruction[6:0]
  // Probe on instruction[31:7]
  Demultiplexer #(.width(25)) demultiplexer_1 (
    .out0(demultiplexer_1_out0), .in(instruction[31:7]), .sel(instruction[2]));  // open: out1
  Demultiplexer #(.select(3), .width(25)) demultiplexer_2 (
    .out0(demultiplexer_2_out0), .out1(demultiplexer_2_out1), .out2(demultiplexer_2_out2),
    .out3(demultiplexer_2_out3), .out6(demultiplexer_2_out6), .in(demultiplexer_1_out0),
    .sel(instruction[6:4]));  // open: out4, out5, out7
  fmt_i load (.instruction(demultiplexer_2_out0), .rd(load_rd), .rs1(load_rs1));  // open: funct3, imm_11_0
  fmt_i alu_immediate (
    .instruction(demultiplexer_2_out1), .rd(alu_immediate_rd), .rs1(alu_immediate_rs1));  // open: funct3, imm_11_0
  fmt_s store (
    .instruction(demultiplexer_2_out2), .rs1(store_rs1), .rs2(store_rs2));  // open: imm_4_0, funct3, imm_11_5
  fmt_r alu (.instruction(demultiplexer_2_out3), .rd(alu_rd), .rs1(alu_rs1), .rs2(alu_rs2));  // open: funct3, funct7
  fmt_b branch (
    .instruction(demultiplexer_2_out6), .rs1(branch_rs1), .rs2(branch_rs2));  // open: imm_4_1_11, funct3, imm_12_10_5
  Multiplexer #(.select(3), .width(5)) multiplexer_1 (
    .in0(load_rd), .in1(alu_immediate_rd), .in3(alu_rd), .sel(instruction[6:4]));  // open: in2, in4, in5, in6, in7, out
  Multiplexer #(.select(3), .width(5)) multiplexer_2 (
    .in0(load_rs1), .in1(alu_immediate_rs1), .in2(store_rs1), .in3(alu_rs1), .in6(branch_rs1),
    .sel(instruction[6:4]));  // open: in4, in5, in7, out
  Multiplexer #(.select(3), .width(5)) multiplexer_3 (
    .in2(store_rs2), .in3(alu_rs2), .in6(branch_rs2), .sel(instruction[6:4]));  // open: in0, in1, in4, in5, in7, out
endmodule

module fmt_r (
  input  [24:0] instruction,
  output [4:0] rd,
  output [2:0] funct3,
  output [4:0] rs1,
  output [4:0] rs2,
  output [6:0] funct7
);


  assign funct3 = instruction[7:5];
  assign funct7 = instruction[24:18];
  assign rd = instruction[4:0];
  assign rs1 = instruction[12:8];
  assign rs2 = instruction[17:13];
endmodule

module fmt_i (
  input  [24:0] instruction,
  output [4:0] rd,
  output [2:0] funct3,
  output [4:0] rs1,
  output [11:0] imm_11_0
);


  assign funct3 = instruction[7:5];
  assign imm_11_0 = instruction[24:13];
  assign rd = instruction[4:0];
  assign rs1 = instruction[12:8];
endmodule

module fmt_s (
  input  [24:0] instruction,
  output [4:0] imm_4_0,
  output [2:0] funct3,
  output [4:0] rs1,
  output [4:0] rs2,
  output [6:0] imm_11_5
);


  assign funct3 = instruction[7:5];
  assign imm_4_0 = instruction[4:0];
  assign imm_11_5 = instruction[24:18];
  assign rs1 = instruction[12:8];
  assign rs2 = instruction[17:13];
endmodule

module fmt_b (
  input  [24:0] instruction,
  output [4:0] imm_4_1_11,
  output [2:0] funct3,
  output [4:0] rs1,
  output [4:0] rs2,
  output [6:0] imm_12_10_5
);


  assign funct3 = instruction[7:5];
  assign imm_4_1_11 = instruction[4:0];
  assign imm_12_10_5 = instruction[24:18];
  assign rs1 = instruction[12:8];
  assign rs2 = instruction[17:13];
endmodule

module fmt_j (
  input  [24:0] instruction,
  output [4:0] rd,
  output [19:0] imm_20_10_1_11_19_12
);


  assign imm_20_10_1_11_19_12 = instruction[24:5];
  assign rd = instruction[4:0];
endmodule

module fmt_u (
  input  [24:0] instruction,
  output [4:0] rd,
  output [19:0] imm_31_12
);


  assign imm_31_12 = instruction[24:5];
  assign rd = instruction[4:0];
endmodule
